// Logisim project digitron2.circ as structural Verilog: 1 circuit, main circuit main
module main (
  input  in_1,
  input  in_2,
  input  in_3,
  input  in_4,
  input  in_5,
  input  in_6,
  input  in_7,
  input  in_8,
  input  in_9,
  output out_10,
  output out_11,
  output out_12,
  output out_13,
  output out_14
);

  wire nand_3_out, nand_4_out, nand_6_out, nand_7_out, nand_8_out, not_3_out, not_4_out, or_2_out;

  // NAND_Gate nand_1 is placed but not wired
  // NOT_Gate not_1 is placed but not wired
  // AND_Gate and_1 is placed but not wired
  // XOR_Gate xor_1 is placed but not wired
  // OR_Gate or_1 is placed but not wired
  nand nand_2 (out_10, in_1, in_1);
  not not_2 (out_11, nand_3_out);
  nand nand_3 (nand_3_out, in_2, in_3);
  not not_3 (not_3_out, in_8);
  not not_4 (not_4_out, in_9);
  or or_2 (or_2_out, in_5, in_7);
  and and_2 (out_13, or_2_out, nand_4_out);
  nand nand_4 (nand_4_out, in_5, in_7);
  nand nand_5 (out_14, not_3_out, not_4_out);
  nand nand_6 (nand_6_out, in_4, in_6);
  nand nand_7 (nand_7_out, in_4, nand_6_out);
  nand nand_8 (nand_8_out, nand_6_out, in_6);
  nand nand_9 (out_12, nand_7_out, nand_8_out);

  // Notes on the sheet:
  //   NAND
  //   NOT
  //   AND
  //   XOR
  //   OR
endmodule
